# Fritzing sketch Equema3 (saved by Fritzing 0.9.3b)
breadboards: 1

parts:
  Componente3 = Arduino Uno (Rev3)
  Q1 = PNP-Transistor [package="TO92 [THT]"]
  Q2 = PNP-Transistor [package="TO92 [THT]"]
  Q3 = PNP-Transistor [package="TO92 [THT]"]
  Q4 = PNP-Transistor [package="TO92 [THT]"]
  Q5 = PNP-Transistor [package="TO92 [THT]"]
  Q6 = PNP-Transistor [package="TO92 [THT]"]
  Q7 = PNP-Transistor [package="TO92 [THT]"]
  Q8 = PNP-Transistor [package="TO92 [THT]"]
  Q9 = PNP-Transistor [package="TO92 [THT]"]
  Q10 = PNP-Transistor [package="TO92 [THT]"]
  R2 = Resistor [tolerance=±5% resistance=10k package=THT]
  R3 = Resistor [tolerance=±5% resistance=10k package=THT]
  R4 = Resistor [tolerance=±5% resistance=10k package=THT]
  R5 = Resistor [tolerance=±5% resistance=10k package=THT]
  R6 = Resistor [tolerance=±5% resistance=10k package=THT]
  R7 = Resistor [tolerance=±5% resistance=10k package=THT]
  R8 = Resistor [tolerance=±5% resistance=10k package=THT]
  R9 = Resistor [tolerance=±5% resistance=10k package=THT]
  R10 = Resistor [tolerance=±5% resistance=10k package=THT]
  R11 = Resistor [tolerance=±5% resistance=10k package=THT]

nets:
  N1: Componente3.D8, Q6.C
  N2: Componente3.D9_PWM, Q8.C
  N3: Componente3.D10_PWM/SS, Q9.C
  N4: Componente3.D11_PWM/MOSI, Q10.C
  N5: Componente3.D2, Q2.C
  N6: Componente3.D3_PWM, Q4.C
  N7: Componente3.D4, Q3.C
  N8: Componente3.D5_PWM, Q5.C
  N9: Componente3.D6_PWM, Q7.C
  N10: Componente3.D7, Q1.C
  N11: Componente3.5V, Q1.E, Q2.E, Q3.E, Q4.E, Q5.E, Q6.E, Q7.E, Q8.E, Q9.E, Q10.E
  N12: Q1.B, R7.Pin_1
  N13: Q2.B, R2.Pin_1
  N14: Q3.B, R4.Pin_1
  N15: Q4.B, R3.Pin_1
  N16: Q5.B, R5.Pin_1
  N17: Q6.B, R8.Pin_1
  N18: Q7.B, R6.Pin_1
  N19: Q8.B, R9.Pin_1
  N20: Q9.B, R10.Pin_1
  N21: Q10.B, R11.Pin_1

notes:
  Rotational control
  control of movements
  Serial Interface
