# Fritzing sketch Esquema2 (saved by Fritzing 0.9.3b)
breadboards: 1

parts:
  LCD1 = LCD screen
  Componente1 = Arduino Uno (Rev3)
  R1 = Trimmer Potentiometer [maximum_resistance=10kΩ package=THT]

nets:
  VSS: LCD1.VSS, LCD1.R/W, LCD1.LED-, Componente1.GND, R1.leg2
  VDD: LCD1.VDD, LCD1.LED+, Componente1.5V, R1.leg1
  N1: LCD1.V0, R1.wiper
  N2: LCD1.RS, Componente1.D7
  N3: LCD1.E, Componente1.D6_PWM
  N4: LCD1.DB4, Componente1.D5_PWM
  N5: LCD1.DB5, Componente1.D4
  N6: LCD1.DB6, Componente1.D3_PWM
  N7: LCD1.DB7, Componente1.D2

notes:
  Serial Interface
